// Logisim project ddca log expo.circ as structural Verilog: 1 circuit, main circuit main
module main (
  input  in_1,
  input  in_2,
  input  in_3,
  input  in_4,
  input  in_5,
  input  in_6,
  input  in_7,
  input  in_8,
  input  in_9,
  output out_10,
  output out_11,
  output out_12,
  output out_13
);

  wire xor_1_out, xor_2_out, xor_3_out, xor_4_out;

  xor xor_1 (xor_1_out, in_3, in_6);
  Adder #(.width(1)) adder_1 (.a(in_1), .b(in_1), .cin(xor_1_out), .cout(out_10));  // open: out
  Adder #(.width(1)) adder_2 (.a(in_1), .b(in_1), .cin(xor_2_out), .cout(out_12));  // open: out
  xor xor_2 (xor_2_out, in_2, in_7);
  Adder #(.width(1)) adder_3 (.a(in_1), .b(in_1), .cin(xor_3_out), .cout(out_11));  // open: out
  xor xor_3 (xor_3_out, in_4, in_8);
  Adder #(.width(1)) adder_4 (.a(xor_4_out), .b(xor_4_out), .cin(xor_4_out), .cout(out_13));  // open: out
  xor xor_4 (xor_4_out, in_5, in_9);
endmodule
